# Fritzing sketch prjAlarmeComBotoes (saved by Fritzing 0.9.2b)
breadboards: 1

parts:
  Componente1 = Arduino Uno (Rev3)
  LED1 = LED - 5mm [color="Green (555nm)" package="5 mm [THT]"]  # not connected
  R1 = Resistor [tolerance=±5% resistance=330 package=THT]  # not connected
  LED2 = LED - 5mm [color="Red (633nm)" package="5 mm [THT]"]
  R2 = Resistor [tolerance=±5% resistance=330 package=THT]
  S1 = Reed switch [package=THT]
  R3 = Resistor [tolerance=±5% resistance=10k package=THT]
  J1 = Piezo Speaker
  KY-1 = Keyes Relay [package=THT]
  PIR1 = PIR sensor
  S2 = Pushbutton [package="[THT]"]
  S3 = Pushbutton [package="[THT]"]
  R4 = Resistor [tolerance=±5% resistance=10k package=THT]
  R5 = Resistor [tolerance=±5% resistance=10k package=THT]

nets:
  5V: Componente1.D8, Componente1.5V, R3.Pin_1, KY-1.signal, PIR1.VDD, PIR1.SIG, S2.Pin_1, S2.Pin_2, S3.Pin_1, S3.Pin_2
  N1: Componente1.D12/MISO, R2.Pin_1
  N2: Componente1.D2, S1.pin_2, R3.Pin_0
  N3: Componente1.D3_PWM, S2.Pin_3, S2.Pin_4, R4.Pin_1
  N4: Componente1.D4, S3.Pin_3, S3.Pin_4, R5.Pin_1
  N5: Componente1.D5_PWM, KY-1.ground
  GND: Componente1.GND, LED2.cathode, S1.pin_1, KY-1.power, PIR1.GND, R4.Pin_0, R5.Pin_0
  N6: Componente1.VIN, KY-1.NO
  N7: LED2.anode, R2.Pin_0
  N8: J1.pin2, KY-1.C

notes:
  Botão Desligar
  BotãoLigar

custom parts:
  Keyes Relay: The Keyes 5V relay module is suitable for SCM development, home appliance control. It uses a 5V~12V TIL control signal which can control DC / AC signal.
